// Logisim project alu-harness.circ as structural Verilog: 1 circuit, main circuit main
module main (
  output [7:0] Test_num,
  output Equal,
  output Signed_Overflow,
  output [31:0] Result,
  output [31:0] toHi,
  output Stall_Pipeline
);

  wire Clock, rom_4_data;
  wire [5:0] rom_3_data;
  wire [7:0] adder_1_out;
  wire [31:0] rom_1_data, rom_2_data;

  Clock clock_1 (.out(Clock));
  Adder adder_1 (.a(8'h1), .b(Test_num), .out(adder_1_out));  // open: cin, cout
  Register register_1 (.D(adder_1_out), .Q(Test_num), .clk(Clock));  // open: en, clr
  ROM #(.dataWidth(32)) rom_1 (.addr(Test_num), .data(rom_1_data));  // open: sel
  ROM #(.dataWidth(32)) rom_2 (.addr(Test_num), .data(rom_2_data));  // open: sel
  ROM #(.dataWidth(6)) rom_3 (.addr(Test_num), .data(rom_3_data));  // open: sel
  ROM #(.dataWidth(1)) rom_4 (.addr(Test_num), .data(rom_4_data));  // open: sel
  alu_main main_1 (
    .Switch__S(rom_3_data), .X(rom_1_data), .Equal(Equal), .RESULT(Result),
    .Signed_Overflow(Signed_Overflow), .Y(rom_2_data), .toHi(toHi), .Stall_Pipeline(Stall_Pipeline),
    .Clock(Clock), .Mul_Div_Reset(rom_4_data));

  // Notes on the sheet:
  //   contents of rom_1 (hex, n*v repeats v):
  //   abcd1234 1234abcd abcd1234 abcd1234 abcd1234 11664166 c0208412 1237357c abcd1234 11664166 c0208412
  //   1237357c 38c70c4 a7445240 4d6a8fd 87445240 38c70c4 a7445240 4d6a8fd 87445240 10300b81 a2dfe3
  //   ffffffff 80000000 10300b81 a2dfe3 ffffffff 80000000 95bbc52 134ac405 93fbbfd 36c8b2d 95bbc52
  //   134ac405 93fbbfd 36c8b2d 38c70c4 a7445240 4d6a8fd a7445240 38c70c4 a7445240 4d6a8fd a7445240
  //   contents of rom_2 (hex, n*v repeats v):
  //   1 10 20 ffffffff 1 5 20 ffffffff 1 5 20 ffffffff 4d6a8fd 38c70c4 b40df210 f40df210 4d6a8fd 38c70c4
  //   b40df210 f40df210 a2dfe3 10300b81 1 1 a2dfe3 10300b81 1 1 5cbbf0 117d30c7 6cb5b7d cbe6934d 5cbbf0
  //   117d30c7 6cb5b7d cbe6934d 4d6a8fd 38c70c4 b40df210 b40df210 4d6a8fd 38c70c4 b40df210 b40df210
  //   contents of rom_3 (hex, n*v repeats v):
  //   4*0 4*2 4*3 4*20 4*21 4*22 4*23 4*24 4*25 4*2a 4*2b
  //   YOUR ALU SHOULD FIT HERE
  //   There should be no blue/red wires here, and the result shouldn't be x's.
endmodule
