// Logisim project alu.circ as structural Verilog: 1 circuit, main circuit main
module main (
  input  [31:0] X,
  input  [31:0] Y,
  input  Clock,
  input  Mul_Div_Reset,
  input  [5:0] Switch__S,
  output Equal,
  output Signed_Overflow,
  output [31:0] RESULT,
  output [31:0] toHi,
  output Stall_Pipeline
);


  // Notes on the sheet:
  //   INPUTS to your circuit
  //   INPUT to your circuit
  //   DON'T CHANGE THE INPUTS AND OUTPUTS! IF YOU DO SO, YOU NEED TO MAKE SURE THE PINS ARE IN THE RIGHT PLACES!
  //   OUTPUTS of your circuit
endmodule
