// Logisim project cpu.circ as structural Verilog: 1 circuit, main circuit main
module main (
  input  [31:0] RS_READ_VALUE,
  input  [31:0] RT_READ_VALUE,
  input  [31:0] INSTRUCTION,
  input  CLOCK,
  input  RESET,
  output [31:0] Lo,
  output [31:0] Hi,
  output [31:0] t0,
  output [31:0] t1,
  output [31:0] t2,
  output [31:0] t3,
  output [4:0] RS,
  output [4:0] RT,
  output [4:0] Write_Register,
  output [31:0] RD_WRITE_VALUE,
  output RD_WRITE_ENABLE,
  output [23:0] FETCH_ADDRESS
);

  wire add, addi, addiu, addu, ALU_signed_overflow, ALUSrc, \and , and_1_out, and_2_out, and_3_out,
       and_9_out, and_10_out, and_11_out, andi, beq, bne, branch_t, comparator_1_lt, comparator_2_lt,
       comparator_3_lt, comparator_4_lt, comparator_21_eq, comparator_22_eq, comparator_23_eq,
       comparator_24_eq, comparator_25_eq, comparator_26_lt, comparator_27_lt, comparator_28_eq,
       comparator_29_eq, comparator_30_eq, comparator_31_eq, comparator_32_eq, comparator_33_eq,
       comparator_34_eq, comparator_35_eq, comparator_36_eq, comparator_37_eq, comparator_38_eq,
       comparator_39_eq, comparator_40_eq, divsub, equal, itype_add, jal, jr, jump, lb, lbu, lui, lw,
       mem_to_reg, mfhi, mflo, mulad, nop, not_1_out, not_2_out, \or , or_2_out, or_3_out, or_4_out,
       or_5_out, or_7_out, or_8_out, or_11_out, or_13_out, ori, rtype, shift, sll, slt, sltu, sra, srl,
       stall, sub, subu, sw, ZeroExt;
  wire [1:0] multiplexer_4_out;
  wire [4:0] multiplexer_16_out;
  wire [5:0] ALUCtr, \function , multiplexer_15_out, multiplexer_17_out, multiplexer_19_out;
  wire [15:6] immediate;
  wire [23:0] adder_1_out, adder_2_out, adder_3_out, bit_extender_5_out, IF_EX_q, multiplexer_10_out,
       multiplexer_12_out, multiplexer_14_out, subtractor_1_out;
  wire [31:0] ALU_rlt, ALU_tohi, bit_extender_1_out, bit_extender_2_out, bit_extender_3_out,
       MEM_data_mem_out, multiplexer_3_out, multiplexer_5_out, multiplexer_6_out, multiplexer_7_out,
       multiplexer_8_out, multiplexer_9_out, multiplexer_11_out, ra_val, rs_val_all, rs_val_t0_3, rt_val_all,
       rt_val_t0_3;
  wire [31:26] INSTRUCTION_t;

  Comparator #(.width(5)) comparator_1 (.a(5'b00111), .b(RS), .lt(comparator_1_lt));  // open: gt, eq
  Comparator #(.width(5)) comparator_2 (.a(RS), .b(5'b01100), .lt(comparator_2_lt));  // open: gt, eq
  Comparator #(.width(5)) comparator_3 (.a(5'b00111), .b(RT), .lt(comparator_3_lt));  // open: gt, eq
  Comparator #(.width(5)) comparator_4 (.a(RT), .b(5'b01100), .lt(comparator_4_lt));  // open: gt, eq
  not not_1 (not_1_out, stall);
  Comparator #(.width(6)) comparator_5 (.a(INSTRUCTION_t), .b({6{1'b0}}), .eq(rtype));  // open: gt, lt
  Comparator #(.width(6)) comparator_6 (.a(INSTRUCTION_t), .b(6'b000010), .eq(jump));  // open: gt, lt
  Comparator #(.width(6)) comparator_7 (.a(INSTRUCTION_t), .b(6'b000011), .eq(jal));  // open: gt, lt
  Comparator #(.width(6)) comparator_8 (.a(INSTRUCTION_t), .b(6'b000100), .eq(beq));  // open: gt, lt
  Comparator #(.width(6)) comparator_9 (.a(INSTRUCTION_t), .b(6'b000101), .eq(bne));  // open: gt, lt
  and and_1 (and_1_out, comparator_1_lt, comparator_2_lt);
  and and_2 (and_2_out, comparator_3_lt, comparator_4_lt);
  assign bit_extender_1_out = {{16{immediate[15]}}, {immediate, \function }};  // Bit_Extender bit_extender_1
  assign bit_extender_2_out = {{16{1'b0}}, {immediate, \function }};  // Bit_Extender bit_extender_2
  Register #(.width(24)) PC (.D(multiplexer_14_out), .en(not_1_out), .Q(FETCH_ADDRESS), .clk(CLOCK));  // open: clr
  Comparator #(.width(6)) comparator_10 (.a(INSTRUCTION_t), .b(6'b001000), .eq(addi));  // open: gt, lt
  Comparator #(.width(6)) comparator_11 (.a(INSTRUCTION_t), .b(6'b001001), .eq(addiu));  // open: gt, lt
  Comparator #(.width(6)) comparator_12 (.a(INSTRUCTION_t), .b(6'b001100), .eq(andi));  // open: gt, lt
  Comparator #(.width(6)) comparator_13 (.a(INSTRUCTION_t), .b(6'b100011), .eq(lw));  // open: gt, lt
  Comparator #(.width(6)) comparator_14 (.a(INSTRUCTION_t), .b(6'b010000), .eq(mfhi));  // open: gt, lt
  Comparator #(.width(6)) comparator_15 (.a(INSTRUCTION_t), .b(6'b010010), .eq(mflo));  // open: gt, lt
  Multiplexer #(.width(32), .enable("false")) multiplexer_1 (
    .in0(RS_READ_VALUE), .in1(rs_val_t0_3), .out(rs_val_all), .sel(and_1_out));
  Multiplexer #(.width(32), .enable("false")) multiplexer_2 (
    .in0(RT_READ_VALUE), .in1(rt_val_t0_3), .out(rt_val_all), .sel(and_2_out));
  Multiplexer #(.width(32), .enable("false")) multiplexer_3 (
    .in0(bit_extender_1_out), .in1(bit_extender_2_out), .out(multiplexer_3_out), .sel(ZeroExt));
  Adder #(.width(24)) adder_1 (.a(FETCH_ADDRESS), .b(24'h1), .out(adder_1_out));  // open: cin, cout
  Multiplexer #(.width(2), .enable("false")) multiplexer_4 (
    .in0(RT[1:0]), .in1(immediate[12:11]), .out(multiplexer_4_out), .sel(rtype));
  or or_1 (shift, sll, srl, sra);
  Multiplexer #(.width(32), .enable("false")) multiplexer_5 (
    .in0(rt_val_all), .in1(multiplexer_3_out), .out(multiplexer_5_out), .sel(ALUSrc));
  Adder #(.width(24)) adder_2 (.a(adder_1_out), .b(24'h100000), .out(adder_2_out));  // open: cin, cout
  Register #(.width(24)) IF_EX (.D(adder_1_out), .Q(IF_EX_q), .clk(CLOCK), .clr(or_2_out));  // open: en
  or or_2 (or_2_out, nop, stall);
  Multiplexer #(.width(32), .enable("false")) multiplexer_6 (
    .in0(INSTRUCTION), .in1({32{1'b0}}), .out(multiplexer_6_out), .sel(nop));
  Comparator #(.width(6)) comparator_16 (.a(INSTRUCTION_t), .b(6'b001101), .eq(ori));  // open: gt, lt
  Comparator #(.width(6)) comparator_17 (.a(INSTRUCTION_t), .b(6'b001111), .eq(lui));  // open: gt, lt
  Comparator #(.width(6)) comparator_18 (.a(INSTRUCTION_t), .b(6'b100000), .eq(lb));  // open: gt, lt
  Comparator #(.width(6)) comparator_19 (.a(INSTRUCTION_t), .b(6'b101011), .eq(sw));  // open: gt, lt
  Comparator #(.width(6)) comparator_20 (.a(INSTRUCTION_t), .b(6'b100100), .eq(lbu));  // open: gt, lt
  and and_3 (and_3_out, RD_WRITE_ENABLE, and_11_out);
  or or_3 (or_3_out, shift, lui);
  Multiplexer #(.width(32), .enable("false")) multiplexer_7 (
    .in0(rs_val_all), .in1(multiplexer_5_out), .out(multiplexer_7_out), .sel(or_3_out));
  Multiplexer #(.width(32), .enable("false")) multiplexer_8 (
    .in0(multiplexer_5_out), .in1(32'h10), .out(multiplexer_8_out), .sel(lui));
  Multiplexer #(.width(32), .enable("false")) multiplexer_9 (
    .in0(multiplexer_8_out), .in1(bit_extender_3_out), .out(multiplexer_9_out), .sel(shift));
  assign bit_extender_3_out = {{27{1'b0}}, immediate[10:6]};  // Bit_Extender bit_extender_3
  or or_4 (or_4_out, lb, lbu);
  assign ra_val = {{8{1'b0}}, adder_2_out};  // Bit_Extender bit_extender_4
  assign bit_extender_5_out = {{8{immediate[15]}}, {immediate, \function }};  // Bit_Extender bit_extender_5
  Register #(.width(32)) register_1 (
    .D(multiplexer_6_out), .Q({INSTRUCTION_t, RS, RT, immediate, \function }), .clk(CLOCK), .clr(or_5_out));  // open: en
  or or_5 (or_5_out, stall, nop);
  regfile_main RegFile (
    .Read_register_1(RS[1:0]), .Read_register_2(RT[1:0]), .write_register(multiplexer_4_out),
    .write_data(RD_WRITE_VALUE), .t0_Value(t0), .t1_Value(t1), .t2_Value(t2), .t3_Value(t3),
    .RegWrite(and_3_out), .clock(CLOCK), .Read_Data_1(rs_val_t0_3), .Read_Data_2(rt_val_t0_3));
  alu_main ALU (
    .Switch__S(ALUCtr), .X(multiplexer_7_out), .Equal(equal), .RESULT(ALU_rlt),
    .Signed_Overflow(ALU_signed_overflow), .Y(multiplexer_9_out), .toHi(ALU_tohi), .Stall_Pipeline(stall),
    .Clock(CLOCK), .Mul_Div_Reset(RESET));
  mem_main MEM (
    .Data_Mem_Addr(ALU_rlt), .Data_Mem_In(rt_val_all), .ACCESS_BYTE(or_4_out), .MEM_WRITE(sw), .CLOCK(CLOCK),
    .Data_Mem_Out(MEM_data_mem_out));
  Adder #(.width(24)) adder_3 (.a(IF_EX_q), .b(bit_extender_5_out), .out(adder_3_out));  // open: cin, cout
  Multiplexer #(.width(24), .enable("false")) multiplexer_10 (
    .in0({RS[2:0], RT, immediate, \function }), .in1(rs_val_all[23:0]), .out(multiplexer_10_out), .sel(jr));
  LED led_1 (.in(ALU_signed_overflow));
  Multiplexer #(.width(32), .enable("false")) multiplexer_11 (
    .in0(ALU_rlt), .in1(MEM_data_mem_out), .out(multiplexer_11_out), .sel(mem_to_reg));
  Multiplexer #(.width(24), .enable("false")) multiplexer_12 (
    .in0(adder_1_out), .in1(adder_3_out), .out(multiplexer_12_out), .sel(branch_t));
  Subtractor #(.width(24)) subtractor_1 (
    .a(multiplexer_10_out), .b(24'h100000), .out(subtractor_1_out));  // open: bin, bout
  or or_6 (ZeroExt, \and , \or );
  not not_2 (not_2_out, equal);
  and and_4 (sll, rtype, comparator_21_eq);
  Comparator #(.width(6)) comparator_21 (.a(\function ), .b({6{1'b0}}), .eq(comparator_21_eq));  // open: gt, lt
  and and_5 (srl, rtype, comparator_22_eq);
  Comparator #(.width(6)) comparator_22 (.a(\function ), .b(6'b000010), .eq(comparator_22_eq));  // open: gt, lt
  and and_6 (sra, rtype, comparator_23_eq);
  Comparator #(.width(6)) comparator_23 (.a(\function ), .b(6'b000011), .eq(comparator_23_eq));  // open: gt, lt
  and and_7 (jr, rtype, comparator_24_eq);
  Comparator #(.width(6)) comparator_24 (.a(\function ), .b(6'b001000), .eq(comparator_24_eq));  // open: gt, lt
  and and_8 (slt, rtype, comparator_25_eq);
  Comparator #(.width(6)) comparator_25 (.a(\function ), .b(6'b101010), .eq(comparator_25_eq));  // open: gt, lt
  Comparator #(.width(5)) comparator_26 (.a(5'b00111), .b(Write_Register), .lt(comparator_26_lt));  // open: gt, eq
  Comparator #(.width(5)) comparator_27 (.a(Write_Register), .b(5'b01100), .lt(comparator_27_lt));  // open: gt, eq
  Comparator #(.width(6)) comparator_28 (.a(6'b111110), .b(ALUCtr), .eq(comparator_28_eq));  // open: gt, lt
  or or_7 (or_7_out, comparator_28_eq, comparator_29_eq);
  Comparator #(.width(6)) comparator_29 (.a(ALUCtr), .b({6{1'b1}}), .eq(comparator_29_eq));  // open: gt, lt
  Multiplexer #(.width(32), .enable("false")) multiplexer_13 (
    .in0(multiplexer_11_out), .in1(ra_val), .out(RD_WRITE_VALUE), .sel(jal));
  or or_8 (or_8_out, jump, jal);
  Multiplexer #(.width(24), .enable("false")) multiplexer_14 (
    .in0(multiplexer_12_out), .in1(subtractor_1_out), .out(multiplexer_14_out), .sel(or_8_out));
  nor nor_1 (ALUSrc, rtype, jump, jal);
  nor nor_2 (RD_WRITE_ENABLE, beq, bne, sw, jump, jr);
  or or_9 (mem_to_reg, lb, lw, lbu);
  and and_9 (and_9_out, beq, equal);
  or or_10 (branch_t, and_9_out, and_10_out);
  and and_10 (and_10_out, not_2_out, bne);
  and and_11 (and_11_out, comparator_26_lt, comparator_27_lt);
  Register #(.width(32)) u_Hi (.D(ALU_tohi), .en(comparator_29_eq), .Q(Hi), .clk(CLOCK));  // open: clr
  Register #(.width(32)) u_Lo (.D(ALU_rlt), .en(or_7_out), .Q(Lo), .clk(CLOCK));  // open: clr
  Multiplexer #(.width(6), .enable("false")) multiplexer_15 (
    .in0({6{1'b0}}), .in1(6'b100101), .out(multiplexer_15_out), .sel(ori));
  and and_12 (mfhi, rtype, comparator_30_eq);
  Comparator #(.width(6)) comparator_30 (.a(\function ), .b(6'b010000), .eq(comparator_30_eq));  // open: gt, lt
  and and_13 (mflo, rtype, comparator_31_eq);
  Comparator #(.width(6)) comparator_31 (.a(\function ), .b(6'b010010), .eq(comparator_31_eq));  // open: gt, lt
  and and_14 (add, rtype, comparator_32_eq);
  Comparator #(.width(6)) comparator_32 (.a(\function ), .b(6'b100000), .eq(comparator_32_eq));  // open: gt, lt
  and and_15 (addu, rtype, comparator_33_eq);
  Comparator #(.width(6)) comparator_33 (.a(\function ), .b(6'b100001), .eq(comparator_33_eq));  // open: gt, lt
  and and_16 (sltu, rtype, comparator_34_eq);
  Comparator #(.width(6)) comparator_34 (.a(\function ), .b(6'b101011), .eq(comparator_34_eq));  // open: gt, lt
  Multiplexer #(.width(5), .enable("false")) multiplexer_16 (
    .in0(RT), .in1(immediate[15:11]), .out(multiplexer_16_out), .sel(rtype));
  Multiplexer #(.width(6), .enable("false")) multiplexer_17 (
    .in0(multiplexer_15_out), .in1(6'b100100), .out(multiplexer_17_out), .sel(andi));
  Multiplexer #(.width(5), .enable("false")) multiplexer_18 (
    .in0(multiplexer_16_out), .in1({5{1'b1}}), .out(Write_Register), .sel(jal));
  or or_11 (or_11_out, addi, addiu, lb);
  or or_12 (itype_add, or_11_out, or_13_out);
  or or_13 (or_13_out, lbu, lw, sw);
  Multiplexer #(.width(6), .enable("false")) multiplexer_19 (
    .in0(multiplexer_17_out), .in1(6'b100000), .out(multiplexer_19_out), .sel(itype_add));
  or or_14 (nop, jump, jal, branch_t);
  Comparator #(.width(6)) comparator_35 (.a(\function ), .b(6'b100010), .eq(comparator_35_eq));  // open: gt, lt
  Comparator #(.width(6)) comparator_36 (.a(\function ), .b(6'b100011), .eq(comparator_36_eq));  // open: gt, lt
  Comparator #(.width(6)) comparator_37 (.a(\function ), .b(6'b100100), .eq(comparator_37_eq));  // open: gt, lt
  Comparator #(.width(6)) comparator_38 (.a(\function ), .b(6'b100101), .eq(comparator_38_eq));  // open: gt, lt
  Comparator #(.width(6)) comparator_39 (.a(\function ), .b(6'b111110), .eq(comparator_39_eq));  // open: gt, lt
  Comparator #(.width(6)) comparator_40 (.a(\function ), .b({6{1'b1}}), .eq(comparator_40_eq));  // open: gt, lt
  Multiplexer #(.width(6), .enable("false")) multiplexer_20 (
    .in0(multiplexer_19_out), .in1(\function ), .out(ALUCtr), .sel(rtype));
  and and_17 (sub, rtype, comparator_35_eq);
  and and_18 (subu, rtype, comparator_36_eq);
  and and_19 (\and , rtype, comparator_37_eq);
  and and_20 (\or , rtype, comparator_38_eq);
  and and_21 (mulad, rtype, comparator_39_eq);
  and and_22 (divsub, rtype, comparator_40_eq);

  // Other names for the same wires on the sheet: clk = CLOCK; fetch_addr[23:0] = FETCH_ADDRESS;
  //   immediate[5:0] = \function ; INSTRUCTION_t[25:0] = {RS, RT, immediate, \function };
  //   j_addr[25:0] = {RS, RT, immediate, \function }; shamt[4:0] = immediate[10:6]; rd[4:0] = immediate[15:11];
  //   opcode[5:0] = INSTRUCTION_t; RS_VAL[31:0] = RS_READ_VALUE; rst = RESET; RT_VAL[31:0] = RT_READ_VALUE;
  //   write_en = RD_WRITE_ENABLE; write_reg[4:0] = Write_Register; write_val[31:0] = RD_WRITE_VALUE

  // Notes on the sheet:
  //   These are outputs/inputs from run.circ
  //   Instruction Decode
  //   Register Read
  //   Execute
  //   Memory
  //   PC Control
  //   These are outputs to run.circ
  //   Control Signals
  //   Instruction Fetch
endmodule
