// Logisim project alu.circ as structural Verilog: 4 circuits, main circuit main
module main (
  input  [31:0] X,
  input  [31:0] Y,
  input  Clock,
  input  Mul_Div_Reset,
  input  [5:0] Switch__S,
  output Equal,
  output Signed_Overflow,
  output [31:0] RESULT,
  output [31:0] toHi,
  output Stall_Pipeline
);

  wire and_1_out, and_2_out, and_3_out, and_4_out, and_6_out, and_7_out, comparator_4_lt, comparator_5_lt,
       divsubu_func, mulad_func, register_3_q, should_stall_divsubu, should_stall_mul;
  wire [4:0] bit_extender_1_out;
  wire [31:0] add, adder_1_out, and_5_out, bit_extender_2_out, bit_extender_3_out, counter_1_q, divsubu,
       mulad, multiplexer_1_out, or_2_out, shifter_1_out, shifter_2_out, shifter_3_out, sub, subtractor_2_out;

  Counter #(.width(32), .max('hffffffff)) counter_1 (
    .count(1'b1), .Q(counter_1_q), .clk(Clock), .clr(Mul_Div_Reset));  // open: load, D, carry
  Comparator #(.width(32)) comparator_1 (.a(counter_1_q), .b(Y), .lt(should_stall_mul));  // open: gt, eq
  Comparator #(.width(6), .mode("unsigned")) comparator_2 (
    .a(6'b111110), .b(Switch__S), .eq(mulad_func));  // open: gt, lt
  Comparator #(.width(6), .mode("unsigned")) comparator_3 (
    .a(Switch__S), .b({6{1'b1}}), .eq(divsubu_func));  // open: gt, lt
  Register #(.width(32)) register_1 (
    .D(adder_1_out), .en(should_stall_mul), .Q(mulad), .clk(Clock), .clr(Mul_Div_Reset));
  and and_1 (and_1_out, ~X[31], ~Y[31], add[31]);  // AND_Gate
  and and_2 (and_2_out, X[31], Y[31], ~add[31]);  // AND_Gate
  and and_3 (and_3_out, X[31], ~Y[31], ~sub[31]);  // AND_Gate
  and and_4 (and_4_out, sub[31], Y[31], ~X[31]);  // AND_Gate
  Adder #(.width(32)) adder_1 (.a(X), .b(mulad), .out(adder_1_out));  // open: cin, cout
  or or_1 (Signed_Overflow, and_1_out, and_2_out, and_3_out, and_4_out);
  Register #(.width(32)) register_2 (
    .D(subtractor_2_out), .en(should_stall_divsubu), .Q(toHi), .clk(Clock));  // open: clr
  Multiplexer #(.width(32), .enable("false")) multiplexer_1 (
    .in0(toHi), .in1(X), .out(multiplexer_1_out), .sel(register_3_q));
  Register #(.width(1)) register_3 (.D(1'b1), .Q(register_3_q), .clk(Mul_Div_Reset), .clr(Clock));  // open: en
  Bit_Extender #(.in_width(32), .out_width(5)) bit_extender_1 (.in(Y), .out(bit_extender_1_out));
  Shifter #(.width(32)) shifter_1 (.in(X), .\dist (bit_extender_1_out), .out(shifter_1_out));
  Shifter #(.width(32), .shift("lr")) shifter_2 (.in(X), .\dist (bit_extender_1_out), .out(shifter_2_out));
  Shifter #(.width(32), .shift("ar")) shifter_3 (.in(X), .\dist (bit_extender_1_out), .out(shifter_3_out));
  Adder #(.width(32)) adder_2 (.a(X), .b(Y), .out(add));  // open: cin, cout
  Subtractor #(.width(32)) subtractor_1 (.a(X), .b(Y), .out(sub));  // open: bin, bout
  assign and_5_out = X & Y;  // AND_Gate and_5, 32 bits wide
  assign or_2_out = X | Y;  // OR_Gate or_2, 32 bits wide
  Comparator #(.width(32)) comparator_4 (.a(X), .b(Y), .lt(comparator_4_lt));  // open: gt, eq
  assign bit_extender_2_out = {{31{1'b0}}, comparator_4_lt};  // Bit_Extender bit_extender_2
  Comparator #(.width(32), .mode("unsigned")) comparator_5 (.a(X), .b(Y), .lt(comparator_5_lt));  // open: gt, eq
  assign bit_extender_3_out = {{31{1'b0}}, comparator_5_lt};  // Bit_Extender bit_extender_3
  Subtractor #(.width(32)) subtractor_2 (.a(multiplexer_1_out), .b(Y), .out(subtractor_2_out));  // open: bin, bout
  Multiplexer #(.select(5), .width(32), .enable("false")) multiplexer_2 (
    .in0(shifter_1_out), .in2(shifter_2_out), .in3(shifter_3_out), .in16(add), .in17(add), .in18(sub),
    .in19(sub), .in20(and_5_out), .in21(or_2_out), .in26(bit_extender_2_out), .in27(bit_extender_3_out),
    .in30(mulad), .in31(divsubu), .out(RESULT), .sel({Switch__S[5], Switch__S[3:0]}));  // open: in1, in4, in5, in6, in7, in8, in9, in10, in11, in12, in13, in14, in15, in22, in23, in24, in25, in28, in29
  Counter #(.width(32), .max('hffffffff)) counter_2 (
    .count(should_stall_divsubu), .Q(divsubu), .clk(Clock), .clr(Mul_Div_Reset));  // open: load, D, carry
  Comparator #(.width(32)) comparator_6 (
    .a(subtractor_2_out), .b({32{1'b0}}), .gt(should_stall_divsubu));  // open: eq, lt
  and and_6 (and_6_out, mulad_func, should_stall_mul);
  Comparator #(.width(32)) comparator_7 (.a(X), .b(Y), .eq(Equal));  // open: gt, lt
  or or_3 (Stall_Pipeline, and_6_out, and_7_out);
  and and_7 (and_7_out, should_stall_divsubu, divsubu_func);

  // Other names for the same wires on the sheet: clk = Clock; oflw = Signed_Overflow; reset = Mul_Div_Reset;
  //   ALUSel[4:0] = {Switch__S[5], Switch__S[3:0]}; x_input[31:0] = X; y_input[31:0] = Y

  // Notes on the sheet:
  //   INPUTS to your circuit
  //   INPUT to your circuit
  //   MULAD (Multiply by Addition)
  //   DON'T CHANGE THE INPUTS AND OUTPUTS! IF YOU DO SO, YOU NEED TO MAKE SURE THE PINS ARE IN THE RIGHT PLACES!
  //   DIVSUB (Division by Subtraction)
  //   OUTPUTS of your circuit
endmodule

module mulad_next (
  input  Reset,
  input  Clock,
  input  [31:0] Limit,
  output IsCounting
);

  wire comparator_1_eq, comparator_1_lt;
  wire [31:0] adder_1_out, register_1_q;

  Register #(.width(32)) register_1 (.D(adder_1_out), .Q(register_1_q), .clk(Clock), .clr(Reset));  // open: en
  Adder #(.width(32)) adder_1 (.a(32'h1), .b(register_1_q), .out(adder_1_out));  // open: cin, cout
  Comparator #(.width(32)) comparator_1 (
    .a(register_1_q), .b(Limit), .eq(comparator_1_eq), .lt(comparator_1_lt));  // open: gt
  or or_1 (IsCounting, comparator_1_lt, comparator_1_eq);

  // Other names for the same wires on the sheet: clk = Clock; rst = Reset

  // Notes on the sheet:
  //   INPUTS
  //   OUTPUTS
endmodule

module dibsub_next (
  input  [31:0] B,
  input  [31:0] Quotient,
  output IsCounting
);

  wire comparator_1_eq, comparator_1_gt;

  Comparator #(.width(32)) comparator_1 (.a(Quotient), .b(B), .gt(comparator_1_gt), .eq(comparator_1_eq));  // open: lt
  or or_1 (IsCounting, comparator_1_gt, comparator_1_eq);

  // Other names for the same wires on the sheet: quot[31:0] = Quotient; rt[31:0] = B

  // Notes on the sheet:
  //   INPUTS
  //   OUTPUTS
endmodule

module divsub (
  input  [31:0] A,
  input  [31:0] B,
  input  Clock,
  input  Reset,
  output [31:0] Remainder,
  output Stall_Pipeline,
  output [31:0] Quotient
);

  wire comparator_1_eq, comparator_1_gt, or_1_out;
  wire [31:0] adder_1_out, multiplexer_1_out, register_1_q, subtractor_1_out;

  Subtractor #(.width(32)) subtractor_1 (.a(Remainder), .b(register_1_q), .out(subtractor_1_out));  // open: bin, bout
  Register #(.width(32)) register_1 (.D(B), .Q(register_1_q), .clk(Clock), .clr(Reset));  // open: en
  Register #(.width(32)) register_2 (.D(adder_1_out), .Q(Quotient), .clk(Clock), .clr(Reset));  // open: en
  Multiplexer #(.width(32), .enable("false")) multiplexer_1 (
    .in0(subtractor_1_out), .in1(A), .out(multiplexer_1_out), .sel(Reset));
  Register #(.width(32)) register_3 (.D(multiplexer_1_out), .en(or_1_out), .Q(Remainder), .clk(Clock));  // open: clr
  or or_1 (or_1_out, Stall_Pipeline, Reset);
  dibsub_next dibsub_next_1 (.B(register_1_q), .IsCounting(Stall_Pipeline));  // open: Quotient
  Comparator #(.width(32)) comparator_1 (
    .a(Remainder), .b(register_1_q), .gt(comparator_1_gt), .eq(comparator_1_eq));  // open: lt
  Adder #(.width(32)) adder_1 (.a(32'h1), .b(Quotient), .out(adder_1_out));  // open: cin, cout
  or or_2 (Stall_Pipeline, comparator_1_gt, comparator_1_eq);

  // Other names for the same wires on the sheet: clk = Clock; shouldStall = Stall_Pipeline

  // Notes on the sheet:
  //   INPUTS
  //   IMPLEMENT A/B
  //   OUTPUTS
endmodule
